# Fritzing sketch moon-patroller (saved by Fritzing 0.9.3b)

parts:
  Part1 = Arduino Uno (Rev3)
  BREAKOUT1 = ULN2003A breakout board
  BREAKOUT2 = ULN2003A breakout board
  MOTOR1 = 28BYJ-48 Stepper Motor  # not connected
  MOTOR2 = 28BYJ-48 Stepper Motor  # not connected
  HC-SR04_Sensor_1 = HC-SR04 Ultrasonic Distance Sensor
  VCC1 = Battery block 9V
  S1 = Toggle Switch [package=THT]

nets:
  N1: Part1.D8, BREAKOUT1.In_3
  N2: Part1.D9_PWM, BREAKOUT1.In_1
  N3: Part1.D10_PWM/SS, BREAKOUT1.In_2
  N4: Part1.D11_PWM/MOSI, BREAKOUT1.In_4
  GND: Part1.GND, BREAKOUT1.0V, BREAKOUT2.0V, HC-SR04_Sensor_1.GND, VCC1.-
  N5: Part1.D2, HC-SR04_Sensor_1.TRIG
  N6: Part1.D3_PWM, HC-SR04_Sensor_1.ECHO
  N7: Part1.D4, BREAKOUT2.In_4
  N8: Part1.D5_PWM, BREAKOUT2.In_2
  N9: Part1.D6_PWM, BREAKOUT2.In_3
  N10: Part1.D7, BREAKOUT2.In_1
  5V: Part1.5V, HC-SR04_Sensor_1.VCC
  +5V: Part1.VIN, BREAKOUT1.+5V, BREAKOUT2.+5V, S1.L1
  N11: VCC1.+, S1.COM

notes:
  I used a small breakout board but didn't want to complicate the diagram with it.

custom parts:
  ULN2003A breakout board: ULN2003A 7-way Darlington Transistor Driver on breakoutboard
